// Logisim project CPU_v24 bits.circ as structural Verilog: 2 circuits, main circuit main
module main (
  input  in_1
);

  wire adder_1_cout, and_1_out, and_2_out, and_3_out, and_5_out, and_6_out, and_7_out, and_8_out, and_9_out,
       and_10_out, clock_1_out, comparator_2_eq, comparator_3_eq, comparator_4_eq, comparator_5_eq,
       comparator_6_eq, comparator_7_eq, comparator_8_eq, counter_2_carry, counter_3_carry,
       demultiplexer_1_out0, demultiplexer_1_out1, demultiplexer_1_out2, demultiplexer_1_out3,
       demultiplexer_1_out4, demultiplexer_1_out5, demultiplexer_1_out6, demultiplexer_1_out7,
       demultiplexer_1_out8, demultiplexer_1_out9, demultiplexer_1_out10, demultiplexer_1_out11,
       demultiplexer_1_out12, demultiplexer_1_out13, demultiplexer_1_out14, demultiplexer_1_out15,
       GLOBAL_RESET_out, multiplexer_4_out, multiplexer_5_out, multiplexer_6_out, multiplexer_8_out,
       multiplexer_9_out, multiplexer_11_out, not_2_out, not_3_out, not_4_out, not_5_out, not_6_out,
       not_7_out, not_8_out, not_9_out, or_1_out, or_5_out, or_7_out, subtractor_1_bout, subtractor_3_bout,
       xnor_1_out, xor_1_out, xor_2_out, xor_3_out;
  wire [1:0] demultiplexer_4_out1_2, demultiplexer_4_out3_2, or_6_out;
  wire [2:0] CODE_ROM_data_4, CODE_ROM_data_7, counter_2_q, dualram_2_p3, subtractor_3_out;
  wire [3:0] BANK_q, bit_extender_5_out, FLAGS_q;
  wire [3:1] comparator_1_eq;
  wire [4:0] counter_2_q_2, counter_3_q, demultiplexer_3_out6, demultiplexer_3_out7, multiplexer_12_out,
       multiplexer_13_out, subtractor_4_out;
  wire [4:3] CODE_ROM_data_5;
  wire [5:0] adder_3_out, adder_4_out, bit_extender_1_out, bit_extender_2_out, bit_extender_6_out,
       COMPOSITOR_q, PIXEL_OFFSET_q, shifter_3_out, subtractor_2_out;
  wire [5:3] CODE_ROM_data_8;
  wire [6:0] demultiplexer_4_out1, demultiplexer_4_out3;
  wire [7:0] A_out, multiplexer_15_out, RINPT_q, STACK_POINTER_q;
  wire [8:0] CODE_ROM_data_3, demultiplexer_4_out2, demultiplexer_4_out4;
  wire [11:0] dualram_1_p11, TILE_OFFSET_q;
  wire [11:10] multiplexer_10_out_2;
  wire [15:0] bit_extender_4_out, demultiplexer_5_out0, demultiplexer_5_out1, rom_1_data, shifter_4_out;
  wire [21:0] multiplexer_10_out;
  wire [23:0] adder_1_out, adder_2_out, and_4_out, bit_extender_3_out, CODE_ROM_data,
       controlled_buffer_1_out, controlled_buffer_2_out, controlled_buffer_3_out, controlled_buffer_4_out,
       counter_1_q, demultiplexer_2_out0, demultiplexer_2_out1, demultiplexer_2_out2, demultiplexer_2_out3,
       demultiplexer_2_out4, demultiplexer_2_out5, demultiplexer_2_out6, demultiplexer_2_out7,
       demultiplexer_3_out0, demultiplexer_3_out1, demultiplexer_3_out2, demultiplexer_3_out3,
       demultiplexer_3_out4, GEN_RAM_dout, multiplexer_1_out, multiplexer_2_out, multiplexer_3_out,
       multiplexer_7_out, not_1_out, or_4_out, R0_q, R1_q, R2_q, R3_q, R4_q, R5_q, R6_q, R7_q, R8_q, R9_q,
       R10_q, R11_q, R12_q, R13_q, R14_q, R15_q, shifter_1_out, shifter_2_out, STACK_dout, subtractor_1_out,
       xor_4_out;
  wire [23:5] demultiplexer_3_out6_2, demultiplexer_3_out7_2;
  wire [25:14] CODE_ROM_data_6;
  wire [31:24] CODE_ROM_data_2;
  wire [63:0] dualram_3_p35, multiplexer_14_out, RESOURCES_ROM_data, shifter_5_out, undriven;

  or or_1 (or_1_out, demultiplexer_4_out1[0], demultiplexer_4_out2[0]);
  Demultiplexer #(.select(4)) demultiplexer_1 (
    .out0(demultiplexer_1_out0), .out1(demultiplexer_1_out1), .out2(demultiplexer_1_out2),
    .out3(demultiplexer_1_out3), .out4(demultiplexer_1_out4), .out5(demultiplexer_1_out5),
    .out6(demultiplexer_1_out6), .out7(demultiplexer_1_out7), .out8(demultiplexer_1_out8),
    .out9(demultiplexer_1_out9), .out10(demultiplexer_1_out10), .out11(demultiplexer_1_out11),
    .out12(demultiplexer_1_out12), .out13(demultiplexer_1_out13), .out14(demultiplexer_1_out14),
    .out15(demultiplexer_1_out15), .in(or_1_out), .sel(CODE_ROM_data_6[25:22]));
  Clock clock_1 (.out(clock_1_out));
  Button GLOBAL_RESET (.out(GLOBAL_RESET_out));
  Register #(.width(24)) R0 (
    .D({multiplexer_10_out_2, multiplexer_10_out}), .en(demultiplexer_1_out0), .Q(R0_q), .clk(clock_1_out),
    .clr(GLOBAL_RESET_out));
  Register #(.width(24)) R4 (
    .D({multiplexer_10_out_2, multiplexer_10_out}), .en(demultiplexer_1_out4), .Q(R4_q), .clk(clock_1_out),
    .clr(GLOBAL_RESET_out));
  Register #(.width(24)) R8 (
    .D({multiplexer_10_out_2, multiplexer_10_out}), .en(demultiplexer_1_out8), .Q(R8_q), .clk(clock_1_out),
    .clr(GLOBAL_RESET_out));
  Register #(.width(24)) R12 (
    .D({multiplexer_10_out_2, multiplexer_10_out}), .en(demultiplexer_1_out12), .Q(R12_q), .clk(clock_1_out),
    .clr(GLOBAL_RESET_out));
  assign controlled_buffer_1_out = demultiplexer_4_out1[1] ? multiplexer_2_out : 24'bz;  // Controlled_Buffer controlled_buffer_1
  assign controlled_buffer_2_out = demultiplexer_4_out1[1] ? multiplexer_3_out : 24'bz;  // Controlled_Buffer controlled_buffer_2
  and and_1 (and_1_out, xor_1_out, xnor_1_out);
  Demultiplexer #(.select(3), .width(24)) demultiplexer_2 (
    .out0(demultiplexer_2_out0), .out1(demultiplexer_2_out1), .out2(demultiplexer_2_out2),
    .out3(demultiplexer_2_out3), .out4(demultiplexer_2_out4), .out5(demultiplexer_2_out5),
    .out6(demultiplexer_2_out6), .out7(demultiplexer_2_out7), .in(controlled_buffer_1_out),
    .sel(demultiplexer_4_out1[6:4]));
  Demultiplexer #(.select(3), .width(24)) demultiplexer_3 (
    .out0(demultiplexer_3_out0), .out1(demultiplexer_3_out1), .out2(demultiplexer_3_out2),
    .out3(demultiplexer_3_out3), .out4(demultiplexer_3_out4),
    .out6({demultiplexer_3_out6_2, demultiplexer_3_out6}),
    .out7({demultiplexer_3_out7_2, demultiplexer_3_out7}), .in(controlled_buffer_2_out),
    .sel(demultiplexer_4_out1[6:4]));  // open: out5
  Register #(.width(24)) R1 (
    .D({multiplexer_10_out_2, multiplexer_10_out}), .en(demultiplexer_1_out1), .Q(R1_q), .clk(clock_1_out),
    .clr(GLOBAL_RESET_out));
  Register #(.width(24)) R5 (
    .D({multiplexer_10_out_2, multiplexer_10_out}), .en(demultiplexer_1_out5), .Q(R5_q), .clk(clock_1_out),
    .clr(GLOBAL_RESET_out));
  Register #(.width(24)) R9 (
    .D({multiplexer_10_out_2, multiplexer_10_out}), .en(demultiplexer_1_out9), .Q(R9_q), .clk(clock_1_out),
    .clr(GLOBAL_RESET_out));
  Register #(.width(24)) R13 (
    .D({multiplexer_10_out_2, multiplexer_10_out}), .en(demultiplexer_1_out13), .Q(R13_q), .clk(clock_1_out),
    .clr(GLOBAL_RESET_out));
  xor xor_1 (xor_1_out, multiplexer_1_out[23], demultiplexer_2_out0[23]);
  xnor xnor_1 (xnor_1_out, demultiplexer_3_out0[23], demultiplexer_2_out0[23]);
  and and_2 (and_2_out, FLAGS_q[2], demultiplexer_4_out1[3]);
  Register #(.width(24)) R2 (
    .D({multiplexer_10_out_2, multiplexer_10_out}), .en(demultiplexer_1_out2), .Q(R2_q), .clk(clock_1_out),
    .clr(GLOBAL_RESET_out));
  Register #(.width(24)) R6 (
    .D({multiplexer_10_out_2, multiplexer_10_out}), .en(demultiplexer_1_out6), .Q(R6_q), .clk(clock_1_out),
    .clr(GLOBAL_RESET_out));
  Register #(.width(24)) R10 (
    .D({multiplexer_10_out_2, multiplexer_10_out}), .en(demultiplexer_1_out10), .Q(R10_q), .clk(clock_1_out),
    .clr(GLOBAL_RESET_out));
  Register #(.width(24)) R14 (
    .D({multiplexer_10_out_2, multiplexer_10_out}), .en(demultiplexer_1_out14), .Q(R14_q), .clk(clock_1_out),
    .clr(GLOBAL_RESET_out));
  or or_2 (comparator_1_eq[3], and_1_out, and_3_out);
  Register #(.width(24)) R3 (
    .D({multiplexer_10_out_2, multiplexer_10_out}), .en(demultiplexer_1_out3), .Q(R3_q), .clk(clock_1_out),
    .clr(GLOBAL_RESET_out));
  Register #(.width(24)) R7 (
    .D({multiplexer_10_out_2, multiplexer_10_out}), .en(demultiplexer_1_out7), .Q(R7_q), .clk(clock_1_out),
    .clr(GLOBAL_RESET_out));
  Register #(.width(24)) R11 (
    .D({multiplexer_10_out_2, multiplexer_10_out}), .en(demultiplexer_1_out11), .Q(R11_q), .clk(clock_1_out),
    .clr(GLOBAL_RESET_out));
  Register #(.width(24)) R15 (
    .D({multiplexer_10_out_2, multiplexer_10_out}), .en(demultiplexer_1_out15), .Q(R15_q), .clk(clock_1_out),
    .clr(GLOBAL_RESET_out));
  xor xor_2 (xor_2_out, multiplexer_1_out[23], demultiplexer_2_out1[23]);
  and and_3 (and_3_out, xor_2_out, xor_3_out);
  xor xor_3 (xor_3_out, demultiplexer_2_out1[23], demultiplexer_3_out1[23]);
  or or_3 (comparator_1_eq[2], adder_1_cout, subtractor_1_bout);
  Adder #(.width(24)) adder_1 (
    .a(demultiplexer_2_out0), .b(demultiplexer_3_out0), .out(adder_1_out), .cin(and_2_out),
    .cout(adder_1_cout));
  Subtractor #(.width(24)) subtractor_1 (
    .a(demultiplexer_2_out1), .b(demultiplexer_3_out1), .out(subtractor_1_out), .bin(and_2_out),
    .bout(subtractor_1_bout));
  assign and_4_out = demultiplexer_2_out2 & demultiplexer_3_out2;  // AND_Gate and_4, 24 bits wide
  assign or_4_out = demultiplexer_2_out3 | demultiplexer_3_out3;  // OR_Gate or_4, 24 bits wide
  assign xor_4_out = demultiplexer_2_out4 ^ demultiplexer_3_out4;  // XOR_Gate xor_4, 24 bits wide
  assign not_1_out = ~demultiplexer_2_out5;  // NOT_Gate not_1, 24 bits wide
  Shifter #(.width(24)) shifter_1 (.in(demultiplexer_2_out6), .\dist (demultiplexer_3_out6), .out(shifter_1_out));
  Shifter #(.shift("lr"), .width(24)) shifter_2 (
    .in(demultiplexer_2_out7), .\dist (demultiplexer_3_out7), .out(shifter_2_out));
  Comparator #(.mode("unsigned"), .width(24)) comparator_1 (
    .a(multiplexer_1_out), .b({24{1'b0}}), .eq(comparator_1_eq[1]));  // open: gt, lt
  Multiplexer #(.select(3), .width(24)) multiplexer_1 (
    .in0(adder_1_out), .in1(subtractor_1_out), .in2(and_4_out), .in3(or_4_out), .in4(xor_4_out),
    .in5(not_1_out), .in6(shifter_1_out), .in7(shifter_2_out), .out(multiplexer_1_out),
    .sel(demultiplexer_4_out1[6:4]));
  Register #(.width(4)) FLAGS (
    .D({comparator_1_eq, multiplexer_1_out[23]}), .en(demultiplexer_4_out1[2]), .Q(FLAGS_q),
    .clk(clock_1_out), .clr(GLOBAL_RESET_out));
  Multiplexer #(.select(4), .width(24)) multiplexer_2 (
    .in0(R0_q), .in1(R1_q), .in2(R2_q), .in3(R3_q), .in4(R4_q), .in5(R5_q), .in6(R6_q), .in7(R7_q),
    .in8(R8_q), .in9(R9_q), .in10(R10_q), .in11(R11_q), .in12(R12_q), .in13(R13_q), .in14(R14_q),
    .in15(R15_q), .out(multiplexer_2_out), .sel(CODE_ROM_data_6[17:14]));
  Multiplexer #(.select(4), .width(24)) multiplexer_3 (
    .in0(R0_q), .in1(R1_q), .in2(R2_q), .in3(R3_q), .in4(R4_q), .in5(R5_q), .in6(R6_q), .in7(R7_q),
    .in8(R8_q), .in9(R9_q), .in10(R10_q), .in11(R11_q), .in12(R12_q), .in13(R13_q), .in14(R14_q),
    .in15(R15_q), .out(multiplexer_3_out), .sel(CODE_ROM_data_6[21:18]));
  RAM #(.clearpin("true"), .dataWidth(24), .enables("line")) STACK (
    .addr(STACK_POINTER_q), .we(demultiplexer_4_out3[2]), .clk(clock_1_out), .din(adder_2_out),
    .dout(STACK_dout), .clr(GLOBAL_RESET_out));
  Counter STACK_POINTER (
    .count(demultiplexer_4_out3[4]), .Q(STACK_POINTER_q), .up(demultiplexer_4_out3[3]), .clk(clock_1_out),
    .clr(GLOBAL_RESET_out));  // open: load, D, carry
  Adder #(.width(24)) adder_2 (.a(24'h1), .b(counter_1_q), .out(adder_2_out));  // open: cin, cout
  Multiplexer #(.select(2)) multiplexer_4 (
    .in0(FLAGS_q[0]), .in1(FLAGS_q[1]), .in2(FLAGS_q[2]), .in3(FLAGS_q[3]), .out(multiplexer_4_out),
    .sel(demultiplexer_4_out3_2));
  Multiplexer multiplexer_5 (
    .in0(multiplexer_4_out), .in1(not_2_out), .out(multiplexer_5_out), .sel(demultiplexer_4_out3[6]));
  not not_2 (not_2_out, multiplexer_6_out);
  Multiplexer #(.select(2)) multiplexer_6 (
    .in0(FLAGS_q[0]), .in1(FLAGS_q[1]), .in2(FLAGS_q[2]), .in3(FLAGS_q[3]), .out(multiplexer_6_out),
    .sel(demultiplexer_4_out3_2));
  RAM #(.addrWidth(24), .clearpin("true"), .dataWidth(24), .enables("line")) GEN_RAM (
    .addr(controlled_buffer_3_out), .we(demultiplexer_4_out2[1]), .clk(clock_1_out),
    .din(controlled_buffer_4_out), .dout(GEN_RAM_dout), .clr(GLOBAL_RESET_out));
  assign controlled_buffer_3_out = demultiplexer_4_out2[2] ? multiplexer_2_out : 24'bz;  // Controlled_Buffer controlled_buffer_3
  assign controlled_buffer_4_out = demultiplexer_4_out2[2] ? {multiplexer_10_out_2, multiplexer_10_out} : 24'bz;  // Controlled_Buffer controlled_buffer_4
  and and_5 (and_5_out, demultiplexer_4_out3[5], multiplexer_5_out);
  Demultiplexer #(.select(3), .width(9)) demultiplexer_4 (
    .out1({demultiplexer_4_out1_2, demultiplexer_4_out1}), .out2(demultiplexer_4_out2),
    .out3({demultiplexer_4_out3_2, demultiplexer_4_out3}), .out4(demultiplexer_4_out4), .in(CODE_ROM_data_3),
    .sel(CODE_ROM_data_7));  // open: out0, out5, out6, out7
  or or_5 (or_5_out, demultiplexer_4_out3[0], and_5_out);
  Multiplexer #(.width(24)) multiplexer_7 (
    .in0(CODE_ROM_data), .in1(STACK_dout), .out(multiplexer_7_out), .sel(demultiplexer_4_out3[1]));
  Counter #(.max('hffffff), .width(24)) counter_1 (
    .load(or_5_out), .D(multiplexer_7_out), .count(multiplexer_8_out), .Q(counter_1_q), .up(1'b1),
    .clk(clock_1_out), .clr(GLOBAL_RESET_out));  // open: carry
  Multiplexer multiplexer_8 (
    .in0(1'b1), .in1(multiplexer_9_out), .out(multiplexer_8_out), .sel(demultiplexer_4_out4[0]));
  Multiplexer multiplexer_9 (
    .in0(counter_2_carry), .in1(and_10_out), .out(multiplexer_9_out), .sel(demultiplexer_4_out4[1]));
  Multiplexer #(.select(3), .width(24)) multiplexer_10 (
    .in0(multiplexer_1_out), .in1(multiplexer_3_out), .in2(GEN_RAM_dout), .in3(CODE_ROM_data),
    .in4(bit_extender_3_out), .out({multiplexer_10_out_2, multiplexer_10_out}), .sel(CODE_ROM_data_4));  // open: in5, in6, in7
  ROM #(.addrWidth(24), .dataWidth(64)) CODE_ROM (
    .addr(counter_1_q),
    .data({CODE_ROM_data_8, CODE_ROM_data_7, CODE_ROM_data_6, CODE_ROM_data_5, CODE_ROM_data_4, CODE_ROM_data_3, CODE_ROM_data_2, CODE_ROM_data}));
  assign or_6_out = demultiplexer_4_out1_2 | demultiplexer_4_out2[4:3];  // OR_Gate or_6, 2 bits wide
  Register RINPT (.D(A_out), .en(1'b1), .Q(RINPT_q), .clk(clock_1_out), .clr(GLOBAL_RESET_out));
  Button LEFT (.out(A_out[5]));
  Register #(.width(12)) TILE_OFFSET (
    .D({multiplexer_10_out[17:12], multiplexer_10_out[8:3]}), .en(or_6_out[0]), .Q(TILE_OFFSET_q),
    .clk(clock_1_out), .clr(GLOBAL_RESET_out));
  assign bit_extender_1_out = {{1{1'b0}}, counter_3_q};  // Bit_Extender bit_extender_1
  assign bit_extender_2_out = {{5{1'b0}}, subtractor_3_bout};  // Bit_Extender bit_extender_2
  assign bit_extender_3_out = {{16{1'b0}}, RINPT_q};  // Bit_Extender bit_extender_3
  Button UP (.out(A_out[4]));
  Button DOWN (.out(A_out[7]));
  Adder #(.width(6)) adder_3 (.a(TILE_OFFSET_q[5:0]), .b(COMPOSITOR_q), .out(adder_3_out));  // open: cin, cout
  Adder #(.width(6)) adder_4 (.a(TILE_OFFSET_q[11:6]), .b(bit_extender_1_out), .out(adder_4_out));  // open: cin, cout
  Subtractor #(.width(6)) subtractor_2 (
    .a(adder_4_out), .b(bit_extender_2_out), .out(subtractor_2_out));  // open: bin, bout
  Button B (.out(A_out[1]));
  Button RIGHT (.out(A_out[6]));
  Button Y (.out(A_out[3]));
  Button X (.out(A_out[2]));
  Button A (.out(A_out[0]));
  Register #(.width(6)) PIXEL_OFFSET (
    .D({multiplexer_10_out[11:9], multiplexer_10_out[2:0]}), .en(or_6_out[0]), .Q(PIXEL_OFFSET_q),
    .clk(clock_1_out), .clr(GLOBAL_RESET_out));
  // DualRAM #(.addrWidth(12), .asyncread("true"), .clearpin("true"), .dataWidth(12)) dualram_1: pin names not known; wires that end beside it: {subtractor_2_out, adder_3_out}, 1'b0, 1'b1, clock_1_out, multiplexer_10_out[11:0], or_6_out[1], 1'b0, clock_1_out, {multiplexer_10_out_2, multiplexer_10_out[21:12]}, GLOBAL_RESET_out, dualram_1_p11
  Comparator #(.mode("unsigned"), .width(6)) comparator_2 (
    .a({6{1'b0}}), .b(PIXEL_OFFSET_q), .eq(comparator_2_eq));  // open: gt, lt
  not not_3 (not_3_out, comparator_2_eq);
  Register #(.width(4)) BANK (
    .D(multiplexer_10_out[21:18]), .en(or_6_out[0]), .Q(BANK_q), .clk(clock_1_out), .clr(GLOBAL_RESET_out));
  Subtractor #(.width(3)) subtractor_3 (
    .a(dualram_2_p3), .b(PIXEL_OFFSET_q[5:3]), .out(subtractor_3_out), .bout(subtractor_3_bout));  // open: bin
  ROM #(.addrWidth(20), .dataWidth(64)) RESOURCES_ROM (
    .addr({in_1, BANK_q, dualram_1_p11, subtractor_3_out}), .data(RESOURCES_ROM_data));
  Comparator #(.mode("unsigned"), .width(6)) comparator_3 (
    .a(6'b011111), .b(COMPOSITOR_q), .eq(comparator_3_eq));  // open: gt, lt
  Comparator #(.mode("unsigned"), .width(6)) comparator_4 (
    .a(6'b100000), .b(COMPOSITOR_q), .eq(comparator_4_eq));  // open: gt, lt
  not not_4 (not_4_out, multiplexer_11_out);
  Multiplexer multiplexer_11 (.in0(comparator_3_eq), .in1(comparator_4_eq), .out(multiplexer_11_out), .sel(not_3_out));
  assign bit_extender_4_out = {{8{1'b0}}, {8{1'b1}}};  // Bit_Extender bit_extender_4
  assign bit_extender_5_out = {{1{1'b0}}, PIXEL_OFFSET_q[2:0]};  // Bit_Extender bit_extender_5
  assign bit_extender_6_out = {{3{1'b0}}, PIXEL_OFFSET_q[2:0]};  // Bit_Extender bit_extender_6
  Shifter #(.width(6)) shifter_3 (.in(bit_extender_6_out), .\dist (3'b011), .out(shifter_3_out));
  Counter #(.max('h3f), .width(6)) COMPOSITOR (
    .count(not_4_out), .Q(COMPOSITOR_q), .clk(clock_1_out), .clr(or_7_out));  // open: load, D, carry, up
  or or_7 (or_7_out, counter_2_carry, GLOBAL_RESET_out);
  Demultiplexer #(.width(16)) demultiplexer_5 (
    .out0(demultiplexer_5_out0), .out1(demultiplexer_5_out1), .in(shifter_4_out), .sel(dualram_2_p3[0]));
  Shifter #(.shift("rr"), .width(16)) shifter_4 (
    .in(bit_extender_4_out), .\dist (bit_extender_5_out), .out(shifter_4_out));
  Multiplexer #(.width(5)) multiplexer_12 (
    .in0(COMPOSITOR_q[4:0]), .in1(counter_2_q_2), .out(multiplexer_12_out), .sel(dualram_2_p3[0]));
  not not_5 (not_5_out, dualram_2_p3[0]);
  Subtractor #(.width(5)) subtractor_4 (
    .a(COMPOSITOR_q[4:0]), .b(5'b00001), .out(subtractor_4_out));  // open: bin, bout
  Comparator #(.mode("unsigned"), .width(6)) comparator_5 (
    .a(6'b100000), .b(COMPOSITOR_q), .eq(comparator_5_eq));  // open: gt, lt
  not not_6 (not_6_out, comparator_6_eq);
  Comparator #(.mode("unsigned"), .width(6)) comparator_6 (
    .a({6{1'b0}}), .b(COMPOSITOR_q), .eq(comparator_6_eq));  // open: gt, lt
  Shifter #(.shift("rl"), .width(64)) shifter_5 (.in(RESOURCES_ROM_data), .\dist (shifter_3_out), .out(shifter_5_out));
  Multiplexer #(.width(5)) multiplexer_13 (
    .in0(COMPOSITOR_q[4:0]), .in1(counter_2_q_2), .out(multiplexer_13_out), .sel(not_5_out));
  not not_7 (not_7_out, comparator_7_eq);
  Comparator #(.mode("unsigned"), .width(6)) comparator_7 (
    .a(6'b100000), .b(COMPOSITOR_q), .eq(comparator_7_eq));  // open: gt, lt
  not not_8 (not_8_out, comparator_8_eq);
  Comparator #(.mode("unsigned"), .width(6)) comparator_8 (
    .a({6{1'b0}}), .b(COMPOSITOR_q), .eq(comparator_8_eq));  // open: gt, lt
  not not_9 (not_9_out, comparator_5_eq);
  and and_6 (and_6_out, not_9_out, not_5_out);
  and and_7 (and_7_out, not_5_out, not_6_out);
  and and_8 (and_8_out, dualram_2_p3[0], not_7_out);
  and and_9 (and_9_out, dualram_2_p3[0], not_8_out);
  // DualRAM #(.addrWidth(5), .byteenables("byteEnables"), .dataWidth(64), .trigger("falling")) dualram_2: pin names not known; wires that end beside it: multiplexer_12_out, and_6_out, dualram_2_p3[0], clock_1_out, demultiplexer_5_out0[0], demultiplexer_5_out0[1], demultiplexer_5_out0[2], demultiplexer_5_out0[3], demultiplexer_5_out0[4], demultiplexer_5_out0[5], demultiplexer_5_out0[6], demultiplexer_5_out0[7], shifter_5_out
  // DualRAM #(.addrWidth(5), .byteenables("byteEnables"), .dataWidth(64), .trigger("falling")) dualram_3: pin names not known; wires that end beside it: subtractor_4_out, and_7_out, dualram_2_p3[0], clock_1_out, demultiplexer_5_out0[8], demultiplexer_5_out0[9], demultiplexer_5_out0[10], demultiplexer_5_out0[11], demultiplexer_5_out0[12], demultiplexer_5_out0[13], demultiplexer_5_out0[14], demultiplexer_5_out0[15], shifter_5_out, multiplexer_13_out, and_8_out, not_5_out, clock_1_out, demultiplexer_5_out1[0], demultiplexer_5_out1[1], demultiplexer_5_out1[2], demultiplexer_5_out1[3], demultiplexer_5_out1[4], demultiplexer_5_out1[5], demultiplexer_5_out1[6], demultiplexer_5_out1[7], shifter_5_out, subtractor_4_out, and_9_out, not_5_out, clock_1_out, demultiplexer_5_out1[8], demultiplexer_5_out1[9], demultiplexer_5_out1[10], demultiplexer_5_out1[11], dualram_3_p35
  Multiplexer #(.width(64)) multiplexer_14 (
    .in0(undriven), .in1(dualram_3_p35), .out(multiplexer_14_out), .sel(not_5_out));
  ROM #(.dataWidth(16)) rom_1 (.addr(multiplexer_15_out), .data(rom_1_data));
  Multiplexer #(.select(3), .width(8)) multiplexer_15 (
    .in0(multiplexer_14_out[63:56]), .in1(multiplexer_14_out[55:48]), .in2(multiplexer_14_out[47:40]),
    .in3(multiplexer_14_out[39:32]), .in4(multiplexer_14_out[31:24]), .in5(multiplexer_14_out[23:16]),
    .in6(multiplexer_14_out[15:8]), .in7(multiplexer_14_out[7:0]), .out(multiplexer_15_out), .sel(counter_2_q));
  Counter counter_2 (
    .Q({counter_2_q_2, counter_2_q}), .carry(counter_2_carry), .up(1'b1), .clk(clock_1_out),
    .clr(GLOBAL_RESET_out));  // open: load, D, count
  Counter counter_3 (
    .count(counter_2_carry), .Q({counter_3_q, dualram_2_p3}), .carry(counter_3_carry), .up(1'b1),
    .clk(clock_1_out), .clr(GLOBAL_RESET_out));  // open: load, D
  // RGB_Video #(.height(256), .scale(1), .width(256)) rgb_video_1: pin names not known; wires that end beside it: GLOBAL_RESET_out, clock_1_out, 1'b1, {counter_2_q_2, counter_2_q}, {counter_3_q, dualram_2_p3}, rom_1_data
  and and_10 (and_10_out, counter_3_carry, counter_2_carry);

  // Notes on the sheet:
  //   BUS_C
  //   BUS_A
  //   REGS_CONTROL
  //   BUS B
  //   ALU_CONTROL
  //   PC_CONTROL
  //   BUS B
  //   STOP_CONTROL
  //   ALU_CONTROL
  //   MOV_CONTROL
  //   BUS_C
  //   ALU_OUT
  //   contents of CODE_ROM (hex, n*v repeats v):
  //   80006100000c000 80006100000f001 800061000012002 800061000005003 80006100000d004 800061000000005
  //   800061000009006 800061000010007 800061000013008 800061000015009 80006100000d00a 80006100000000b
  //   80006100000400c 80006100000f00d 80006100000c00e 80006100000f00f 800061000012010 800061000000011
  //   800061000013012 800061000009013 800061000014014 800061000000015 800061000001016 80006100000d017
  //   800061000005018 800061000014019 80006100000001a 80006100000301b 80006100000f01c 80006100000e01d
  //   80006100001301e 80006100000501f 800061000003020 800061000014021 800061000005022 800061000014023
  //   800061000015024 800061000012025 800061000000026 800061000001027 800061000004028 800061000009029
  //   80006100001002a 80006100000902b 80006100001302c 80006100000302d 80006100000902e 80006100000e02f
  //   800061000007030 800061000000031 800061000005032 80006100000c033 800061000009034 800061000014035
  //   800061000000036 800061000013037 800061000005038 800061000004039 80006100000003a 80006100000403b
  //   80006100000f03c 80006100000003d 80006100000503e 80006100000903f 800061000015040 800061000013041
  //   80006100000d042 80006100000f043 800061000004044 800061000000045 800061000014046 800061000005047
  //   80006100000d048 800061000010049 80006100000f04a 80006100001204b 80006100000004c 80006100000904d
  //   80006100000e04e 80006100000304f 800061000009050 800061000004051 800061000009052 800061000004053
  //   800061000015054 80006100000e055 800061000014056 800061000000057 800061000015058 800061000014059
  //   80006100000005a 80006100000c05b 80006100000105c 80006100000205d 80006100000f05e 80006100001205f
  //   800061000005060 800061000000061 800061000005062 800061000014063 800061000000064 800061000004065
  //   80006100000f066 80006100000c067 80006100000f068 800061000012069 80006100000506a 80006100000006b
  //   80006100000d06c 80006100000106d 80006100000706e 80006100000e06f 800061000001070 800061000000071
  //   800061000001072 80006100000c073 800061000009074 800061000011075 800061000015076 800061000001077
  //   800061000000078 800061000015079 80006100001407a 80006100000007b 80006100000507c 80006100000e07d
  //   80006100000907e 80006100000d07f 800061000000080 800061000001081 800061000004082 800061000000083
  //   80006100000d084 800061000009085 80006100000e086 800061000009087 80006100000d088 800061000000089
  //   80006100001608a 80006100000508b 80006100000e08c 80006100000908d 80006100000108e 80006100000d08f
  //   800061000000090 800061000011091 800061000015092 800061000009093 800061000013094 800061000000095
  //   80006100000e096 80006100000f097 800061000013098 800061000014099 80006100001209a 80006100001509b
  //   80006100000409c 80006100000009d 80006100000509e 80006100001809f 8000610000050a0 8000610000120a1
  //   8000610000030a2 8000610000090a3 8000610000140a4 8000610000010a5 8000610000140a6 8000610000090a7
  //   80006100000f0a8 80006100000e0a9 8000610000000aa 8000610000150ab 80006100000c0ac 80006100000c0ad
  //   8000610000010ae 80006100000d0af 8000610000030b0 80006100000f0b1 8000610000000b2 80006100000c0b3
  //   8000610000010b4 8000610000020b5 80006100000f0b6 8000610000120b7 8000610000090b8 8000610000130b9
  //   8000610000000ba 80006100000e0bb 8000610000090bc 8000610000130bd 8000610000090be 8000610000000bf
  //   8000610000150c0 8000610000140c1 8000610000000c2 8000610000010c3 80006100000c0c4 8000610000090c5
  //   8000610000110c6 8000610000150c7 8000610000090c8 8000610000100c9 8000610000000ca 8000610000050cb
  //   8000610000180cc 8000610000000cd 8000610000050ce 8000610000010cf 8000610000000d0 8000610000030d1
  //   80006100000f0d2 80006100000d0d3 80006100000d0d4 80006100000f0d5 8000610000040d6 80006100000f0d7
  //   8000610000000d8 8000610000030d9 80006100000f0da 80006100000e0db 8000610000130dc 8000610000050dd
  //   8000610000110de 8000610000150df 8000610000010e0 8000610000140e1 8000610000000e2 8000610000040e3
  //   8000610000150e4 8000610000090e5 8000610000130e6 8000610000000e7 8000610000010e8 8000610000150e9
  //   8000610000140ea 8000610000050eb 8000610000000ec 8000610000090ed 8000610000120ee 8000610000150ef
  //   8000610000120f0 8000610000050f1 8000610000000f2 8000610000040f3 80006100000f0f4 80006100000c0f5
  //   80006100000f0f6 8000610000120f7 8000610000000f8 8000610000090f9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
  //   FINE_CONTROL
  //   BUS_C_SEL
  //   REGS_CONTROL
  //   OPCODE
  //   contents of RESOURCES_ROM (hex, n*v repeats v):
  //   9*0 c0c0c0c0000 c000000000c00 c000000000c00 c000000000c00 c0c0c0c0c0c00 c000000000c00 c000000000c00
  //   0 c0c0c0c0c0000 c000000000c00 c000000000c00 c0c0c0c0c0000 c000000000c00 c000000000c00 c0c0c0c0c0000
  //   0 c0c0c0c0000 c000000000c00 c000000000000 c000000000000 c000000000000 c000000000c00 c0c0c0c0000 0
  //   c0c0c0c0c0000 5*c000000000c00 c0c0c0c0c0000 0 c0c0c0c0c0000 c000000000000 c000000000000
  //   c0c0c0c0c0000 c000000000000 c000000000000 c0c0c0c0c0000 0 c0c0c0c0c0000 c000000000000 c000000000000
  //   c0c0c0c000000 c000000000000 c000000000000 c000000000000 0 c0c0c000000 c0000000c0000 c000000000000
  //   c000c0c0c0000 c0000000c0000 c0000000c0000 c0c0c000000 0 c0000000c0000 c0000000c0000 c0000000c0000
  //   c0c0c0c0c0000 c0000000c0000 c0000000c0000 c0000000c0000 0 c0c0c0c0c0000 5*c00000000 c0c0c0c0c0000 0
  //   c0c0c0c0c0000 4*c0000 c0000000c0000 c0c0c000000 0 c0000000c0000 c00000c000000 c000c00000000
  //   c0c0000000000 c000c00000000 c00000c000000 c0000000c0000 0 6*c000000000000 c0c0c0c0c0000 0
  //   c0000000c0000 c0c000c0c0000 c000c000c0000 4*c0000000c0000 0 c0000000c0000 c0c00000c0000
  //   c0c00000c0000 c000c000c0000 c000c000c0000 c00000c0c0000 c00000c0c0000 0 c0c0c000000 5*c0000000c0000
  //   c0c0c000000 0 c0c0c0c000000 c0000000c0000 c0000000c0000 c0000000c0000 c0c0c0c000000 c000000000000
  //   c000000000000 0 c0c0c000000 4*c0000000c0000 c00000c0c0000 c0c0c0c0c00 0 c0c0c0c000000 c0000000c0000
  //   c0000000c0000 c0c0c0c000000 c0000000c0000 c0000000c0000 c0000000c0000 0 c0c0c000000 c0000000c0000
  //   c000000000000 c0c0c000000 c0000 c0000000c0000 c0c0c000000 0 c0c0c0c0c0000 6*c00000000 0
  //   6*c0000000c0000 c0c0c000000 0 4*c0000000c0000 c000c000000 c000c000000 c00000000 0 6*c000c000c0000
  //   c000c000000 0 c0000000c0000 c0000000c0000 c000c000000 c00000000 c000c000000 c0000000c0000
  //   c0000000c0000 0 c0000000c0000 c0000000c0000 c0000000c0000 c000c000000 c00000000 c00000000 c00000000
  //   0 c0c0c0c0c0000 c0000 c000000 c00000000 c0000000000 c000000000000 c0c0c0c0c0000 8*c0c0c0c0c0c0c0c
  //   8*1020304050607
  //   contents of rom_1 (hex, n*v repeats v):
  //   18e5 592b b1ea ebea fe6e a78e 3dac 238f 29ad 3af9 453e 777e f7be 9598 5370 31ea
endmodule

module test (
  input  PX_OFFSET,
  input  OAM
);

  wire and_1_out, and_2_out, and_3_out, clock_1_out, counter_1_carry, d_ff_1_q, HBLANK_out, not_1_out,
       not_2_out, or_1_out, or_2_out;

  and and_1 (and_1_out, not_2_out, d_ff_1_q);
  and and_2 (and_2_out, HBLANK_out, PX_OFFSET);
  or or_1 (or_1_out, and_1_out, and_2_out);
  not not_1 (not_1_out, d_ff_1_q);
  D_Flip_Flop d_ff_1 (.clk(clock_1_out), .D(or_1_out), .Q(d_ff_1_q));  // open: Qn, preset, reset
  Button HBLANK (.out(HBLANK_out));
  and and_3 (and_3_out, not_1_out, OAM);
  not not_2 (not_2_out, counter_1_carry);
  Counter #(.max('h1f), .width(5)) counter_1 (
    .count(or_2_out), .carry(counter_1_carry), .clk(clock_1_out));  // open: load, D, Q, up, clr
  or or_2 (or_2_out, HBLANK_out, not_2_out, and_3_out);
  Clock clock_1 (.out(clock_1_out));
  Button button_1 ();  // open: out
endmodule
